// Logisim project LC3-2200a.circ as structural Verilog: 4 circuits, main circuit Datapath
module Datapath (
);

  wire ALUHi, ALULo, CCMatch, Clk, Clr, comparator_1_eq, comparator_1_gt, comparator_1_lt, DrALU, DrMEM,
       DrOFF, DrPC, DrREG, LdA, LdB, LdCC, LdIR, LdMAR, LdPC, N_q, P_q, RegSelHi, RegSelLo, WrMEM, WrREG, Z_q;
  wire [3:0] OP, RegNo, RX, RY, RZ;
  wire [19:4] IR_q;
  wire [31:0] A_q, alu_1_out, B_q, bit_extender_2_out, controlled_buffer_1_out, MAR_q, PC_q, ram_1_data,
       ram_2_data;

  Register #(.width(32)) PC (.D(controlled_buffer_1_out), .en(LdPC), .Q(PC_q), .clk(Clk), .clr(Clr));
  assign controlled_buffer_1_out = DrPC ? PC_q : 32'bz;  // Controlled_Buffer controlled_buffer_1
  Register #(.width(32)) A (.D(controlled_buffer_1_out), .en(LdA), .Q(A_q), .clk(Clk), .clr(Clr));
  ALU alu_1 (.A(A_q), .B(B_q), .func({ALUHi, ALULo}), .Out(alu_1_out));
  Micro_sequencer micro_sequencer_1 (
    .Operation(OP), .CCMatch(CCMatch), .Clk(Clk), .Clr(Clr), .DrREG(DrREG), .DrMEM(DrMEM), .DrALU(DrALU),
    .DrPC(DrPC), .DrOFF(DrOFF), .LdPC(LdPC), .LdIR(LdIR), .LdMAR(LdMAR), .LdA(LdA), .LdB(LdB), .LdCC(LdCC),
    .WrREG(WrREG), .WrMEM(WrMEM), .RegSelLo(RegSelLo), .RegSelHi(RegSelHi), .ALULo(ALULo), .ALUHi(ALUHi));
  Register #(.width(32)) B (.D(controlled_buffer_1_out), .en(LdB), .Q(B_q), .clk(Clk), .clr(Clr));
  assign controlled_buffer_1_out = DrALU ? alu_1_out : 32'bz;  // Controlled_Buffer controlled_buffer_2
  Comparator #(.width(32)) comparator_1 (
    .a(controlled_buffer_1_out), .b({32{1'b0}}), .gt(comparator_1_gt), .eq(comparator_1_eq),
    .lt(comparator_1_lt));
  Register #(.width(1)) P (.D(LdCC), .en(comparator_1_gt), .Q(P_q), .clk(Clk), .clr(Clr));
  RAM #(.addrWidth(4), .dataWidth(32), .bus("separate")) ram_1 (
    .addr(RegNo), .din(controlled_buffer_1_out), .data(ram_1_data), .str(WrREG), .clk(Clk), .ld(1'b1),
    .clr(Clr));  // open: sel
  assign controlled_buffer_1_out = DrREG ? ram_1_data : 32'bz;  // Controlled_Buffer controlled_buffer_3
  Register #(.width(1)) Z (.D(comparator_1_eq), .en(LdCC), .Q(Z_q), .clk(Clk), .clr(Clr));
  Register #(.width(1)) N (.D(comparator_1_lt), .en(LdCC), .Q(N_q), .clk(Clk), .clr(Clr));
  Bit_Extender #(.in_width(32), .out_width(24), .\type ("sign")) bit_extender_1 (.in(MAR_q));  // open: out
  CheckCC checkcc_1 (.N(N_q), .Z(Z_q), .P(P_q), .N_IR(RY[0]), .Z_IR(RY[1]), .P_IR(RY[2]), .CCMatch(CCMatch));
  Register #(.width(32)) MAR (.D(controlled_buffer_1_out), .en(LdMAR), .Q(MAR_q), .clk(Clk), .clr(Clr));
  Register #(.width(32)) IR (.D(controlled_buffer_1_out), .en(LdIR), .Q({OP, RX, RY, IR_q, RZ}), .clk(Clk), .clr(Clr));
  RAM #(.addrWidth(16), .dataWidth(32), .bus("separate")) ram_2 (
    .din(controlled_buffer_1_out), .data(ram_2_data), .str(WrMEM), .clk(Clk), .ld(1'b1));  // open: addr, sel, clr
  assign controlled_buffer_1_out = DrMEM ? ram_2_data : 32'bz;  // Controlled_Buffer controlled_buffer_4
  assign bit_extender_2_out = {{12{IR_q[19]}}, {IR_q, RZ}};  // Bit_Extender bit_extender_2
  assign controlled_buffer_1_out = DrOFF ? bit_extender_2_out : 32'bz;  // Controlled_Buffer controlled_buffer_5
  Clock clock_1 (.out(Clk));
  Button button_1 (.out(Clr));

  // Notes on the sheet:
  //   Registers 16 x 16 bits
  //   Memory 65536 x 16 bit
endmodule

module ALU (
  input  [31:0] A,
  input  [31:0] B,
  input  [1:0] func,
  output [31:0] Out
);

  wire [31:0] a_1, add, \nand , shift, shifter_1_out, shifter_2_out, shifter_3_out;

  assign \nand  = ~(A & B);  // NAND_Gate nand_1, 32 bits wide
  Adder #(.width(32)) adder_1 (.a(A), .b(32'h1), .out(a_1));  // open: cin, cout
  Adder #(.width(32)) adder_2 (.a(A), .b(B), .out(add));  // open: cin, cout
  Multiplexer #(.select(2), .width(32)) multiplexer_1 (
    .in0(add), .in1(\nand ), .in2(a_1), .in3(shift), .out(Out), .sel(func));  // open: en
  Shifter #(.width(32), .shift("lr")) shifter_1 (.in(A), .\dist (B[4:0]), .out(shifter_1_out));
  Shifter #(.width(32), .shift("ar")) shifter_2 (.in(A), .\dist (B[4:0]), .out(shifter_2_out));
  Shifter #(.width(32)) shifter_3 (.in(A), .\dist (B[4:0]), .out(shifter_3_out));
  Multiplexer #(.select(2), .width(32)) multiplexer_2 (
    .in0(shifter_3_out), .in1(shifter_2_out), .in2(shifter_1_out), .out(shift), .sel(B[19:18]));  // open: in3, en

  // Other names for the same wires on the sheet: select[1:0] = func
endmodule

module Micro_sequencer (
  input  [3:0] Operation,
  input  CCMatch,
  input  Clk,
  input  Clr,
  output DrREG,
  output DrMEM,
  output DrALU,
  output DrPC,
  output DrOFF,
  output LdPC,
  output LdIR,
  output LdMAR,
  output LdA,
  output LdB,
  output LdCC,
  output WrREG,
  output WrMEM,
  output RegSelLo,
  output RegSelHi,
  output ALULo,
  output ALUHi
);

  wire chkZ, OPTest;
  wire [1:0] bit_extender_1_out;
  wire [5:0] multiplexer_1_out, rom_1_data, rom_2_data, rom_3_data, State_q;

  assign bit_extender_1_out = {{1{1'b0}}, CCMatch};  // Bit_Extender bit_extender_1
  ROM #(.addrWidth(4), .dataWidth(6)) rom_1 (.addr(Operation), .data(rom_1_data));  // open: sel
  Multiplexer #(.select(2), .width(6)) multiplexer_1 (
    .in0(rom_3_data), .in1(rom_1_data), .in2(rom_2_data), .out(multiplexer_1_out), .sel({chkZ, OPTest}),
    .en(1'b1));  // open: in3
  ROM #(.addrWidth(2), .dataWidth(6)) rom_2 (.addr(bit_extender_1_out), .data(rom_2_data));  // open: sel
  Register #(.width(6)) State (.D(multiplexer_1_out), .Q(State_q), .clk(Clk), .clr(Clk));  // open: en
  ROM #(.addrWidth(6), .dataWidth(25)) rom_3 (
    .addr(State_q),
    .data({chkZ, OPTest, ALUHi, ALULo, RegSelHi, RegSelLo, WrMEM, WrREG, LdCC, LdB, LdA, LdMAR, LdIR, LdPC, DrOFF, DrPC, DrALU, DrMEM, DrREG, rom_3_data}));  // open: sel

  assign Clr = Clk;

  // Notes on the sheet:
  //   contents of rom_1 (hex, n*v repeats v):
  //   3 9 f 13 16 19 1b 1e 22 25
  //   contents of rom_2 (hex, n*v repeats v):
  //   0 b
  //   contents of rom_3 (hex, n*v repeats v):
  //   6201 1082 e00900 4059 8805a 41011b 421c 841d 900 404d 8804e 101000f 4210 8411 8405f 8405f 8420 2121
  //   40040 84044 108045 20100 84047 8408 620100 a0213 840 84063 108064 620100 84055 8416 2117 20080 8404a
  //   10804b 220100
endmodule

module CheckCC (
  input  N,
  input  Z,
  input  P,
  input  N_IR,
  input  Z_IR,
  input  P_IR,
  output CCMatch
);

  wire and_1_out, and_2_out, and_3_out;

  and and_1 (and_1_out, N, N_IR);
  and and_2 (and_2_out, Z, Z_IR);
  or or_1 (CCMatch, and_1_out, and_2_out, and_3_out);
  and and_3 (and_3_out, P, P_IR);
endmodule
